# Fritzing sketch CircuitDiagram (saved by Fritzing 0.9.10b)
breadboards: 1

parts:
  Mini_Ultra_8MHz_Microcontroller = QFN-28 [chip_label="Mini Ultra 8Mhz" package=QFN]
  ZS-042_RTC1 = ZS-042 RTC Module
  3_6V_DC_Power = Battery Holders [package=battery-aa]
  MOSFET_1 = Basic FET N-Channel [package="D2Pak [SMD]"]
  MOSFET_2 = Basic FET N-Channel [package="D2Pak [SMD]"]
  12V_DC_Power_1 = Battery Holders [package=battery-aa]
  LED1 = smd LED [color="Red (633nm)" package="0805 [SMD]"]
  12V_DC_Power_2 = Battery Holders [package=battery-aa]
  M1 = DC Motor [voltage_(max)=6V voltage_(min)=3V]
  M2 = DC Motor [voltage_(max)=6V voltage_(min)=3V]
  S1 = SPST Switch [package=switch-spdt]  # not connected

nets:
  N1: Mini_Ultra_8MHz_Microcontroller.3, MOSFET_1.source
  N2: Mini_Ultra_8MHz_Microcontroller.5, MOSFET_2.source
  N3: Mini_Ultra_8MHz_Microcontroller.13, LED1.cathode
  N4: Mini_Ultra_8MHz_Microcontroller.16, ZS-042_RTC1.GND
  N5: Mini_Ultra_8MHz_Microcontroller.17, ZS-042_RTC1.VCC
  N6: Mini_Ultra_8MHz_Microcontroller.18, 3_6V_DC_Power.-
  N7: Mini_Ultra_8MHz_Microcontroller.26, ZS-042_RTC1.SDA
  N8: Mini_Ultra_8MHz_Microcontroller.27, ZS-042_RTC1.SCL
  N9: MOSFET_1.drain, 12V_DC_Power_1.-
  N10: MOSFET_2.drain, 12V_DC_Power_2.-
  N11: 12V_DC_Power_1.+, M1.pin_1
  N12: 12V_DC_Power_2.+, M2.pin_1
